// Logisim project 1bitadder.circ as structural Verilog: 2 circuits, main circuit main
module main (
  input  [31:0] in_1
);
endmodule

module ALU_1bit (
  input  Binvert,
  input  A,
  input  B,
  input  CarryIn,
  input  [1:0] OpCode,
  output result,
  output C_out
);

  wire adder_1_out, and_1_out, or_1_out, xor_1_out, xor_2_out;

  xor xor_1 (xor_1_out, Binvert, B);
  and and_1 (and_1_out, A, B);
  or or_1 (or_1_out, A, B);
  Adder #(.width(1)) adder_1 (.a(A), .b(xor_1_out), .out(adder_1_out), .cin(CarryIn), .cout(C_out));
  xor xor_2 (xor_2_out, A, B);
  Multiplexer #(.select(2)) multiplexer_1 (
    .in0(and_1_out), .in1(or_1_out), .in2(adder_1_out), .in3(xor_2_out), .out(result), .sel(OpCode));
endmodule
