// Logisim project RiskVAlu.circ as structural Verilog: 2 circuits, main circuit main
module main (
  input  [31:0] A,
  input  [31:0] B,
  input  Binvert,
  input  [1:0] Opselect,
  input  in_5,
  output Is_Zero,
  output [31:0] Result,
  output [31:0] SLT,
  output C_flag
);

  wire alu_1bit_1_c_out, alu_1bit_2_c_out, alu_1bit_3_c_out, alu_1bit_4_c_out, alu_1bit_5_c_out,
       alu_1bit_6_c_out, alu_1bit_7_c_out, alu_1bit_8_c_out, alu_1bit_9_c_out, alu_1bit_10_c_out,
       alu_1bit_11_c_out, alu_1bit_12_c_out, alu_1bit_13_c_out, alu_1bit_14_c_out, alu_1bit_15_c_out,
       alu_1bit_16_c_out, alu_1bit_17_c_out, alu_1bit_18_c_out, alu_1bit_19_c_out, alu_1bit_20_c_out,
       alu_1bit_21_c_out, alu_1bit_22_c_out, alu_1bit_23_c_out, alu_1bit_24_c_out, alu_1bit_26_c_out,
       alu_1bit_27_c_out, alu_1bit_28_c_out, alu_1bit_29_c_out, alu_1bit_30_c_out, alu_1bit_31_c_out,
       alu_1bit_32_c_out;

  ALU_1bit alu_1bit_1 (
    .Binvert(Binvert), .B(B[0]), .A(A[0]), .CarryIn(Binvert), .OpCode(Opselect), .result(Result[0]),
    .C_out(alu_1bit_1_c_out));
  ALU_1bit alu_1bit_2 (
    .Binvert(Binvert), .B(B[1]), .A(A[1]), .CarryIn(alu_1bit_1_c_out), .OpCode(Opselect), .result(Result[1]),
    .C_out(alu_1bit_2_c_out));
  ALU_1bit alu_1bit_3 (
    .Binvert(Binvert), .B(B[2]), .A(A[2]), .CarryIn(alu_1bit_2_c_out), .OpCode(Opselect), .result(Result[2]),
    .C_out(alu_1bit_3_c_out));
  ALU_1bit alu_1bit_4 (
    .Binvert(Binvert), .B(B[3]), .A(A[3]), .CarryIn(alu_1bit_3_c_out), .OpCode(Opselect), .result(Result[3]),
    .C_out(alu_1bit_4_c_out));
  ALU_1bit alu_1bit_5 (
    .Binvert(Binvert), .B(B[4]), .A(A[4]), .CarryIn(alu_1bit_4_c_out), .OpCode(Opselect), .result(Result[4]),
    .C_out(alu_1bit_5_c_out));
  ALU_1bit alu_1bit_6 (
    .Binvert(Binvert), .B(B[5]), .A(A[5]), .CarryIn(alu_1bit_5_c_out), .OpCode(Opselect), .result(Result[5]),
    .C_out(alu_1bit_6_c_out));
  ALU_1bit alu_1bit_7 (
    .Binvert(Binvert), .B(B[6]), .A(A[6]), .CarryIn(alu_1bit_6_c_out), .OpCode(Opselect), .result(Result[6]),
    .C_out(alu_1bit_7_c_out));
  ALU_1bit alu_1bit_8 (
    .Binvert(Binvert), .B(B[7]), .A(A[7]), .CarryIn(alu_1bit_7_c_out), .OpCode(Opselect), .result(Result[7]),
    .C_out(alu_1bit_8_c_out));
  ALU_1bit alu_1bit_9 (
    .Binvert(Binvert), .B(B[16]), .A(A[16]), .CarryIn(alu_1bit_17_c_out), .OpCode(Opselect),
    .result(Result[16]), .C_out(alu_1bit_9_c_out));
  ALU_1bit alu_1bit_10 (
    .Binvert(Binvert), .B(B[17]), .A(A[17]), .CarryIn(alu_1bit_9_c_out), .OpCode(Opselect),
    .result(Result[17]), .C_out(alu_1bit_10_c_out));
  ALU_1bit alu_1bit_11 (
    .Binvert(Binvert), .B(B[18]), .A(A[18]), .CarryIn(alu_1bit_10_c_out), .OpCode(Opselect),
    .result(Result[18]), .C_out(alu_1bit_11_c_out));
  ALU_1bit alu_1bit_12 (
    .Binvert(Binvert), .B(B[19]), .A(A[19]), .CarryIn(alu_1bit_11_c_out), .OpCode(Opselect),
    .result(Result[19]), .C_out(alu_1bit_12_c_out));
  ALU_1bit alu_1bit_13 (
    .Binvert(Binvert), .B(B[20]), .A(A[20]), .CarryIn(alu_1bit_12_c_out), .OpCode(Opselect),
    .result(Result[20]), .C_out(alu_1bit_13_c_out));
  ALU_1bit alu_1bit_14 (
    .Binvert(Binvert), .B(B[21]), .A(A[21]), .CarryIn(alu_1bit_13_c_out), .OpCode(Opselect),
    .result(Result[21]), .C_out(alu_1bit_14_c_out));
  ALU_1bit alu_1bit_15 (
    .Binvert(Binvert), .B(B[22]), .A(A[22]), .CarryIn(alu_1bit_14_c_out), .OpCode(Opselect),
    .result(Result[22]), .C_out(alu_1bit_15_c_out));
  ALU_1bit alu_1bit_16 (
    .Binvert(Binvert), .B(B[23]), .A(A[23]), .CarryIn(alu_1bit_15_c_out), .OpCode(Opselect),
    .result(Result[23]), .C_out(alu_1bit_16_c_out));
  ALU_1bit alu_1bit_17 (
    .Binvert(Binvert), .B(B[15]), .A(A[15]), .CarryIn(alu_1bit_18_c_out), .OpCode(Opselect),
    .result(Result[15]), .C_out(alu_1bit_17_c_out));
  ALU_1bit alu_1bit_18 (
    .Binvert(Binvert), .B(B[14]), .A(A[14]), .CarryIn(alu_1bit_19_c_out), .OpCode(Opselect),
    .result(Result[14]), .C_out(alu_1bit_18_c_out));
  ALU_1bit alu_1bit_19 (
    .Binvert(Binvert), .B(B[13]), .A(A[13]), .CarryIn(alu_1bit_20_c_out), .OpCode(Opselect),
    .result(Result[13]), .C_out(alu_1bit_19_c_out));
  ALU_1bit alu_1bit_20 (
    .Binvert(Binvert), .B(B[12]), .A(A[12]), .CarryIn(alu_1bit_21_c_out), .OpCode(Opselect),
    .result(Result[12]), .C_out(alu_1bit_20_c_out));
  ALU_1bit alu_1bit_21 (
    .Binvert(Binvert), .B(B[11]), .A(A[11]), .CarryIn(alu_1bit_22_c_out), .OpCode(Opselect),
    .result(Result[11]), .C_out(alu_1bit_21_c_out));
  ALU_1bit alu_1bit_22 (
    .Binvert(Binvert), .B(B[10]), .A(A[10]), .CarryIn(alu_1bit_23_c_out), .OpCode(Opselect),
    .result(Result[10]), .C_out(alu_1bit_22_c_out));
  ALU_1bit alu_1bit_23 (
    .Binvert(Binvert), .B(B[9]), .A(A[9]), .CarryIn(alu_1bit_24_c_out), .OpCode(Opselect),
    .result(Result[9]), .C_out(alu_1bit_23_c_out));
  ALU_1bit alu_1bit_24 (
    .Binvert(Binvert), .B(B[8]), .A(A[8]), .CarryIn(alu_1bit_8_c_out), .OpCode(Opselect), .result(Result[8]),
    .C_out(alu_1bit_24_c_out));
  ALU_1bit alu_1bit_25 (
    .Binvert(Binvert), .B(B[31]), .A(A[31]), .CarryIn(alu_1bit_26_c_out), .OpCode(Opselect),
    .result(Result[31]), .C_out(C_flag));
  ALU_1bit alu_1bit_26 (
    .Binvert(Binvert), .B(B[30]), .A(A[30]), .CarryIn(alu_1bit_27_c_out), .OpCode(Opselect),
    .result(Result[30]), .C_out(alu_1bit_26_c_out));
  ALU_1bit alu_1bit_27 (
    .Binvert(Binvert), .B(B[29]), .A(A[29]), .CarryIn(alu_1bit_28_c_out), .OpCode(Opselect),
    .result(Result[29]), .C_out(alu_1bit_27_c_out));
  ALU_1bit alu_1bit_28 (
    .Binvert(Binvert), .B(B[28]), .A(A[28]), .CarryIn(alu_1bit_29_c_out), .OpCode(Opselect),
    .result(Result[28]), .C_out(alu_1bit_28_c_out));
  ALU_1bit alu_1bit_29 (
    .Binvert(Binvert), .B(B[27]), .A(A[27]), .CarryIn(alu_1bit_30_c_out), .OpCode(Opselect),
    .result(Result[27]), .C_out(alu_1bit_29_c_out));
  ALU_1bit alu_1bit_30 (
    .Binvert(Binvert), .B(B[26]), .A(A[26]), .CarryIn(alu_1bit_31_c_out), .OpCode(Opselect),
    .result(Result[26]), .C_out(alu_1bit_30_c_out));
  ALU_1bit alu_1bit_31 (
    .Binvert(Binvert), .B(B[25]), .A(A[25]), .CarryIn(alu_1bit_32_c_out), .OpCode(Opselect),
    .result(Result[25]), .C_out(alu_1bit_31_c_out));
  ALU_1bit alu_1bit_32 (
    .Binvert(Binvert), .B(B[24]), .A(A[24]), .CarryIn(alu_1bit_16_c_out), .OpCode(Opselect),
    .result(Result[24]), .C_out(alu_1bit_32_c_out));
  nor nor_1 (Is_Zero, Result[0], Result[1], Result[2], Result[3], Result[4], Result[5], Result[6], Result[7], Result[8], Result[9], Result[10], Result[11], Result[12], Result[13], Result[14], Result[15], Result[16], Result[17], Result[18], Result[19], Result[20], Result[21], Result[22], Result[23], Result[24], Result[25], Result[26], Result[27], Result[28], Result[29], Result[30], Result[31]);

  assign SLT = {{31{in_5}}, Result[31]};

  // Other names for the same wires on the sheet: op[1:0] = Opselect; sub = Binvert

  // Notes on the sheet:
  //    Opcode Key:
  //   00 : AND
  //   01 : OR
  //   10: XOR
  //   11 : ADD
endmodule

module ALU_1bit (
  input  Binvert,
  input  B,
  input  A,
  input  CarryIn,
  input  [1:0] OpCode,
  output result,
  output C_out
);

  wire adder_1_out, and_1_out, or_1_out, xor_1_out, xor_2_out;

  xor xor_1 (xor_1_out, Binvert, B);
  and and_1 (and_1_out, A, xor_1_out);
  or or_1 (or_1_out, A, xor_1_out);
  Adder #(.width(1)) adder_1 (.a(A), .b(xor_1_out), .out(adder_1_out), .cin(CarryIn), .cout(C_out));
  xor xor_2 (xor_2_out, A, xor_1_out);
  Multiplexer #(.select(2)) multiplexer_1 (
    .in0(and_1_out), .in1(or_1_out), .in2(xor_2_out), .in3(adder_1_out), .out(result), .sel(OpCode));

  // Notes on the sheet:
  //   Opcode Key:
  //   00 : AND
  //   01 : OR
  //   10: XOR
  //   11 : ADD
endmodule
